# Fritzing sketch Artnet DMX Converter (saved by Fritzing 1.0.4)
circuit board: 9cm x 8cm
perfboards: 1

parts:
  XLR1 = XLR NC3MAAH [package=nc3maah]
  XLR2 = XLR NC3MAAH [package=nc3maah]
  C2_100nF = Capacitor [package=cap-pth-5mm]
  C3_100nF = Capacitor [package=cap-pth-5mm]
  X1 = USB Connectors [package=usb-microb]
  Squix1 = OLED 0.96" 128x64 I2C SSD1306
  M1 = MAX485 Breakout [package=THT]
  M2 = MAX485 Breakout [package=THT]
  C2_100nF1 = Capacitor [package=cap-pth-5mm]
  R1 = Resistor [tolerance=±5% power=0.25W resistance=10k package=THT]
  R2 = Resistor [tolerance=±5% power=0.25W resistance=10k package=THT]
  U1 = LuaNode32 / ESP32 [part_number=ESP32S-PIN30]
  C1 = Electrolytic Capacitor [capacitance=1mF voltage=35V package="100 mil [THT, electrolytic]"]

nets:
  GND: XLR1.1, XLR1.G, XLR2.1, XLR2.G, C2_100nF.1, C3_100nF.1, X1.GND, Squix1.GND, M1.GND, M2.GND, C2_100nF1.2, R1.Pin_0, R2.Pin_0, U1.GND, C1.+
  N1: XLR1.2, M1.B
  N2: XLR1.3, M1.A, M1.A1
  N3: XLR2.2, M2.B, M2.B1
  N4: XLR2.3, M2.A, M2.A1
  VCC: C2_100nF.2, X1.VBUS, Squix1.VCC, M1.VCC, C2_100nF1.1, U1.Vin, C1.-
  N5: C3_100nF.2, M2.VCC
  N6: Squix1.SCL, U1.D22
  N7: Squix1.SCA, U1.D21
  N8: M1.RO, U1.D26
  N9: M1.RE, M1.DE, R2.Pin_1, U1.D13
  N10: M1.DI, U1.D25
  N11: M2.RO, R1.Pin_1, U1.D18
  N12: M2.RE, M2.DE, U1.D32
  N13: M2.DI, U1.D19

custom parts:
  MAX485 Breakout: MAX485 RS485 breakout board
  LuaNode32 / ESP32: New Image for LuaNode32 DOIT ESP32 DEVKIT V1. Base parts from LuaNode32 / ESP32 ESP32 based LuaNode32 by G.Noorlander DOIT Esp32 DevKit v1 (30 pins long, 11 pins width) by Werner Rothschopf (modified by vanepp Dec 2018)
